# Fritzing sketch Device_Sketch (saved by Fritzing 0.9.3b)
breadboards: 1

parts:
  U1 = ESP8266 WiFi Module [part_number=ESP8266]
  Part1 = Arduino Uno (Rev3) - ICSP
  LED1 = LEDs [package=led10mm]
  LED2 = LEDs [package=led10mm]
  LED3 = LEDs [package=led10mm]
  R1 = Resistor [tolerance=±5% resistance=220 package=THT]
  R2 = Resistor [tolerance=±5% resistance=220 package=THT]
  R3 = Resistor [tolerance=±5% resistance=220 package=THT]
  S1 = KY-026

nets:
  N1: U1.RXD, Part1.D1/TX
  VCC: U1.VCC, Part1.3V3
  GND: U1.CH_PD, U1.GND, Part1.GND, LED1.C, LED2.C, LED3.C, S1.pin3
  N2: U1.TXD, Part1.D0/RX
  N3: Part1.A0, S1.pin1
  N4: Part1.D8, S1.pin4
  N5: Part1.D3_PWM, R1.Pin_1
  N6: Part1.D4, R2.Pin_1
  N7: Part1.D5_PWM, R3.Pin_1
  N8: Part1.5V, S1.pin2
  N9: LED1.A, R2.Pin_0
  N10: LED2.A, R1.Pin_0
  N11: LED3.A, R3.Pin_0

custom parts:
  ESP8266 WiFi Module: Generic WiFi Module based on the ESP8266 with onboard PCB antenna and UART communications
  KY-026: ky-026 flame sensor module
